// Logisim project ALU.circ as structural Verilog: 19 circuits, main circuit testbench
module testbench (
  input  RorL,
  input  LorA,
  input  [2:0] func_code,
  input  [3:0] Write_Address,
  input  [2:0] B_Read_Address,
  input  [2:0] A_Read_Address,
  input  [7:0] immediate,
  input  clk,
  input  immediate_en,
  output Equal,
  output overflow,
  output [7:0] Result
);

  wire [7:0] register_file_1_a, register_file_1_b;

  // Probe on immediate
  register_file register_file_1 (
    .A_sel(A_Read_Address), .C_sel(Write_Address), .B_sel(B_Read_Address), .immediate_en(immediate_en),
    .Imm(immediate), .C(Result), .clk(clk), .B(register_file_1_b), .A(register_file_1_a));
  // Probe on register_file_1_a
  EqualityDetector equalitydetector_1 (.A(register_file_1_a), .B(register_file_1_b), .Equal(Equal));
  // Probe on register_file_1_b
  // Probe on func_code
  ALU alu_1 (
    .function_code(func_code), .SignExtend(LorA), .RightorLeft(RorL), .A(register_file_1_a),
    .B(register_file_1_b), .D(Result), .over(overflow));
  // Probe on Result

  // Notes on the sheet:
  //   en_b
  //   Register File and ALU
  //   0: Right Shift
  //   1: Left shift
  //   0: Logical Shift
  //   1: Arithmatic Shift
  //   Function Codes ---->
  //   Function Codes
  //   0: Add: A + B
  //   1: Subtract: A - B
  //   2: Bitwise And: A and B
  //   3: Bitwise Or: A or B
  //   4: Bitwise Xor: A xor B
  //   5: Bitwise Nor: A nor B
  //   6: Shift: Shifts A by B number of bits
  //   7: Compare: Compares A with B
  //   Bits 2 to 0: Greater than / Equal to / Less than
endmodule

module NegaFullAdder (
  input  A,
  input  B,
  input  C,
  output S_bar,
  output Cout_bar
);

  wire transistor_1_out, transistor_5_out, transistor_7_out, transistor_10_out, transistor_11_out,
       transistor_14_out, transistor_19_out, transistor_20_out, transistor_23_out, transistor_24_out;

  Transistor transistor_1 (.in(1'b1), .out(transistor_1_out), .gate(A));
  Transistor transistor_2 (.in(1'b1), .out(transistor_1_out), .gate(B));
  Transistor transistor_3 (.in(transistor_1_out), .out(Cout_bar), .gate(C));
  Transistor #(.\type ("n")) transistor_4 (.in(transistor_5_out), .out(Cout_bar), .gate(C));
  Transistor #(.\type ("n")) transistor_5 (.in(1'b0), .out(transistor_5_out), .gate(A));
  Transistor #(.\type ("n")) transistor_6 (.in(1'b0), .out(transistor_5_out), .gate(B));
  Transistor transistor_7 (.in(1'b1), .out(transistor_7_out), .gate(B));
  Transistor transistor_8 (.in(transistor_7_out), .out(Cout_bar), .gate(A));
  Transistor #(.\type ("n")) transistor_9 (.in(transistor_10_out), .out(Cout_bar), .gate(A));
  Transistor #(.\type ("n")) transistor_10 (.in(1'b0), .out(transistor_10_out), .gate(B));
  Transistor transistor_11 (.in(1'b1), .out(transistor_11_out), .gate(A));
  Transistor transistor_12 (.in(transistor_11_out), .out(S_bar), .gate(Cout_bar));
  Transistor #(.\type ("n")) transistor_13 (.in(transistor_14_out), .out(S_bar), .gate(Cout_bar));
  Transistor #(.\type ("n")) transistor_14 (.in(1'b0), .out(transistor_14_out), .gate(A));
  Transistor transistor_15 (.in(1'b1), .out(transistor_11_out), .gate(B));
  Transistor #(.\type ("n")) transistor_16 (.in(1'b0), .out(transistor_14_out), .gate(B));
  Transistor transistor_17 (.in(1'b1), .out(transistor_11_out), .gate(C));
  Transistor #(.\type ("n")) transistor_18 (.in(1'b0), .out(transistor_14_out), .gate(C));
  Transistor transistor_19 (.in(1'b1), .out(transistor_19_out), .gate(C));
  Transistor transistor_20 (.in(transistor_19_out), .out(transistor_20_out), .gate(B));
  Transistor transistor_21 (.in(transistor_20_out), .out(S_bar), .gate(A));
  Transistor #(.\type ("n")) transistor_22 (.in(transistor_23_out), .out(S_bar), .gate(A));
  Transistor #(.\type ("n")) transistor_23 (.in(transistor_24_out), .out(transistor_23_out), .gate(B));
  Transistor #(.\type ("n")) transistor_24 (.in(1'b0), .out(transistor_24_out), .gate(C));
endmodule

module EightBitAdder (
  input  en_b,
  input  K,
  input  [7:0] A,
  input  [7:0] B,
  output [7:0] D,
  output Overflow
);

  wire negafulladder_1_cout_bar, negafulladder_2_cout_bar, negafulladder_3_cout_bar,
       negafulladder_4_cout_bar, negafulladder_5_cout_bar, negafulladder_6_cout_bar,
       negafulladder_7_cout_bar, negafulladder_8_cout_bar, not_1_out, not_2_out, not_3_out, not_4_out,
       not_5_out, not_6_out, not_7_out, not_8_out, xor_1_out, xor_2_out, xor_3_out, xor_4_out, xor_5_out,
       xor_6_out, xor_7_out, xor_8_out, xor_9_out;
  wire [7:0] negafulladder_1_s_bar, not_9_out;

  xor xor_1 (xor_1_out, B[0], K);
  xor xor_2 (xor_2_out, B[1], K);
  xor xor_3 (xor_3_out, B[2], K);
  xor xor_4 (xor_4_out, B[3], K);
  xor xor_5 (xor_5_out, B[4], K);
  xor xor_6 (xor_6_out, B[5], K);
  xor xor_7 (xor_7_out, B[6], K);
  xor xor_8 (xor_8_out, B[7], K);
  NegaFullAdder negafulladder_1 (
    .A(A[0]), .B(xor_1_out), .C(K), .Cout_bar(negafulladder_1_cout_bar), .S_bar(negafulladder_1_s_bar[0]));
  not not_1 (not_1_out, negafulladder_1_cout_bar);
  NegaFullAdder negafulladder_2 (
    .A(A[1]), .B(xor_2_out), .C(not_1_out), .Cout_bar(negafulladder_2_cout_bar),
    .S_bar(negafulladder_1_s_bar[1]));
  not not_2 (not_2_out, negafulladder_2_cout_bar);
  NegaFullAdder negafulladder_3 (
    .A(A[2]), .B(xor_3_out), .C(not_2_out), .Cout_bar(negafulladder_3_cout_bar),
    .S_bar(negafulladder_1_s_bar[2]));
  not not_3 (not_3_out, negafulladder_3_cout_bar);
  NegaFullAdder negafulladder_4 (
    .A(A[3]), .B(xor_4_out), .C(not_3_out), .Cout_bar(negafulladder_4_cout_bar),
    .S_bar(negafulladder_1_s_bar[3]));
  not not_4 (not_4_out, negafulladder_4_cout_bar);
  NegaFullAdder negafulladder_5 (
    .A(A[4]), .B(xor_5_out), .C(not_4_out), .Cout_bar(negafulladder_5_cout_bar),
    .S_bar(negafulladder_1_s_bar[4]));
  not not_5 (not_5_out, negafulladder_5_cout_bar);
  NegaFullAdder negafulladder_6 (
    .A(A[5]), .B(xor_6_out), .C(not_5_out), .Cout_bar(negafulladder_6_cout_bar),
    .S_bar(negafulladder_1_s_bar[5]));
  not not_6 (not_6_out, negafulladder_6_cout_bar);
  NegaFullAdder negafulladder_7 (
    .A(A[6]), .B(xor_7_out), .C(not_6_out), .Cout_bar(negafulladder_7_cout_bar),
    .S_bar(negafulladder_1_s_bar[6]));
  not not_7 (not_7_out, negafulladder_7_cout_bar);
  NegaFullAdder negafulladder_8 (
    .A(A[7]), .B(xor_8_out), .C(not_7_out), .Cout_bar(negafulladder_8_cout_bar),
    .S_bar(negafulladder_1_s_bar[7]));
  not not_8 (not_8_out, negafulladder_8_cout_bar);
  assign not_9_out = ~negafulladder_1_s_bar;  // NOT_Gate not_9, 8 bits wide
  buff8 buff8_1 (.enb(en_b), .A(not_9_out), .Y(D));
  xor xor_9 (xor_9_out, not_8_out, K);
  buf1 buf1_1 (.enb(en_b), .A(xor_9_out), .Y(Overflow));
endmodule

module ALU (
  input  [7:0] A,
  input  [2:0] function_code,
  input  [7:0] B,
  input  SignExtend,
  input  RightorLeft,
  output [7:0] D,
  output over
);

  wire decoder2to4_1_a0, decoder2to4_1_a1, decoder2to4_1_a2, decoder2to4_1_a3, nand_1_out, nand_2_out,
       not_1_out, not_2_out, or_1_out, xor2_1_y;

  not not_1 (not_1_out, xor2_1_y);
  XOR2 xor2_1 (.A(function_code[1]), .B(function_code[2]), .Y(xor2_1_y));
  or or_1 (or_1_out, function_code[1], function_code[2]);
  decoder2to4 decoder2to4_1 (
    .en(not_1_out), .S0(function_code[0]), .S1(function_code[2]), .A0(decoder2to4_1_a0),
    .A1(decoder2to4_1_a1), .A2(decoder2to4_1_a2), .A3(decoder2to4_1_a3));
  not not_2 (not_2_out, function_code[0]);
  nand nand_1 (nand_1_out, not_2_out, function_code[1], function_code[2]);
  nand nand_2 (nand_2_out, function_code[0], function_code[1], function_code[2]);
  EightBitAdder eightbitadder_1 (.K(function_code[0]), .A(A), .B(B), .en_b(or_1_out), .Overflow(over), .D(D));
  and8 and8_1 (.A(A), .B(B), .en_b(decoder2to4_1_a0), .Y(D));
  or8 or8_1 (.A(A), .B(B), .en_b(decoder2to4_1_a1), .Y(D));
  xor8 xor8_1 (.A(A), .B(B), .en_b(decoder2to4_1_a2), .Y(D));
  nor8 nor8_1 (.A(A), .B(B), .en_b(decoder2to4_1_a3), .Y(D));
  Shift shift_1 (.enb(nand_1_out), .A(A), .sign_extend(SignExtend), .shift_amount(B), .RightOrLeft(RightorLeft), .Y(D));
  comparator8bit comparator8bit_1 (.B(B), .A(A), .enb(nand_2_out), .GEL(D));

  // Notes on the sheet:
  //   0: Add
  //   1: Subtract
  //   2: And
  //   3: Or
  //   4: Xor
  //   5: Nor
  //   6: Shift
  //   7: Compare
  //   Function Codes
  //   0: Logical
  //   1: Arithmatic
  //   0: Right
  //   1: Left
  //   Last three bits: Greater/Equal/Less for A compared to B
endmodule

module Shift (
  input  sign_extend,
  input  [7:0] A,
  input  enb,
  input  RightOrLeft,
  input  [7:0] shift_amount,
  output [7:0] Y
);

  wire [1:1] and_2_out, and_3_out, and_4_out;
  wire [7:0] mux8x3_1_y, mux8x3_2_y, mux8x3_3_y;
  wire [7:7] and_1_out;

  and and_1 (and_1_out[7], sign_extend, A[7]);
  and and_2 (and_2_out[1], RightOrLeft, shift_amount[2]);
  mux8x3 mux8x3_1 (
    .C({A[3:0], 4'b0000}), .B({{4{and_1_out[7]}}, A[7:4]}), .A(A), .s({and_2_out[1], shift_amount[2]}),
    .Y(mux8x3_1_y));
  and and_3 (and_3_out[1], RightOrLeft, shift_amount[1]);
  mux8x3 mux8x3_2 (
    .C({mux8x3_1_y[5:0], 2'b00}), .B({{2{and_1_out[7]}}, mux8x3_1_y[7:2]}), .A(mux8x3_1_y),
    .s({and_3_out[1], shift_amount[1]}), .Y(mux8x3_2_y));
  and and_4 (and_4_out[1], RightOrLeft, shift_amount[0]);
  mux8x3 mux8x3_3 (
    .C({mux8x3_2_y[6:0], 1'b0}), .B({and_1_out[7], mux8x3_2_y[7:1]}), .A(mux8x3_2_y),
    .s({and_4_out[1], shift_amount[0]}), .Y(mux8x3_3_y));
  buff8 buff8_1 (.enb(enb), .A(mux8x3_3_y), .Y(Y));
endmodule

module XOR2 (
  input  A,
  input  B,
  output Y
);

  wire A_bar, B_bar, transistor_1_out, transistor_4_out, transistor_5_out, transistor_8_out;

  not not_1 (A_bar, A);
  not not_2 (B_bar, B);
  Transistor transistor_1 (.in(1'b1), .out(transistor_1_out), .gate(A));
  Transistor transistor_2 (.in(transistor_1_out), .out(Y), .gate(B_bar));
  Transistor #(.\type ("n")) transistor_3 (.in(transistor_4_out), .out(Y), .gate(A_bar));
  Transistor #(.\type ("n")) transistor_4 (.in(1'b0), .out(transistor_4_out), .gate(B_bar));
  Transistor transistor_5 (.in(1'b1), .out(transistor_5_out), .gate(A_bar));
  Transistor transistor_6 (.in(transistor_5_out), .out(Y), .gate(B));
  Transistor #(.\type ("n")) transistor_7 (.in(transistor_8_out), .out(Y), .gate(A));
  Transistor #(.\type ("n")) transistor_8 (.in(1'b0), .out(transistor_8_out), .gate(B));
endmodule

module and8 (
  input  [7:0] A,
  input  en_b,
  input  [7:0] B,
  output [7:0] Y
);

  wire [7:0] and_1_out;

  and and_1 (and_1_out[0], A[0], B[0]);
  and and_2 (and_1_out[1], A[1], B[1]);
  and and_3 (and_1_out[2], A[2], B[2]);
  and and_4 (and_1_out[3], A[3], B[3]);
  and and_5 (and_1_out[4], A[4], B[4]);
  and and_6 (and_1_out[5], A[5], B[5]);
  and and_7 (and_1_out[6], A[6], B[6]);
  and and_8 (and_1_out[7], A[7], B[7]);
  buff8 buff8_1 (.enb(en_b), .A(and_1_out), .Y(Y));
endmodule

module or8 (
  input  [7:0] A,
  input  en_b,
  input  [7:0] B,
  output [7:0] Y
);

  wire [7:0] or_1_out;

  or or_1 (or_1_out[0], A[0], B[0]);
  or or_2 (or_1_out[1], A[1], B[1]);
  or or_3 (or_1_out[2], A[2], B[2]);
  or or_4 (or_1_out[3], A[3], B[3]);
  or or_5 (or_1_out[4], A[4], B[4]);
  or or_6 (or_1_out[5], A[5], B[5]);
  or or_7 (or_1_out[6], A[6], B[6]);
  or or_8 (or_1_out[7], A[7], B[7]);
  buff8 buff8_1 (.enb(en_b), .A(or_1_out), .Y(Y));
endmodule

module xor8 (
  input  [7:0] A,
  input  en_b,
  input  [7:0] B,
  output [7:0] Y
);

  wire [7:0] xor2_1_y;

  XOR2 xor2_1 (.A(A[0]), .B(B[0]), .Y(xor2_1_y[0]));
  XOR2 xor2_2 (.A(A[1]), .B(B[1]), .Y(xor2_1_y[1]));
  XOR2 xor2_3 (.A(A[2]), .B(B[2]), .Y(xor2_1_y[2]));
  XOR2 xor2_4 (.A(A[3]), .B(B[3]), .Y(xor2_1_y[3]));
  XOR2 xor2_5 (.A(A[4]), .B(B[4]), .Y(xor2_1_y[4]));
  XOR2 xor2_6 (.A(A[5]), .B(B[5]), .Y(xor2_1_y[5]));
  XOR2 xor2_7 (.A(A[6]), .B(B[6]), .Y(xor2_1_y[6]));
  XOR2 xor2_8 (.A(A[7]), .B(B[7]), .Y(xor2_1_y[7]));
  buff8 buff8_1 (.enb(en_b), .A(xor2_1_y), .Y(Y));
endmodule

module nor8 (
  input  [7:0] A,
  input  en_b,
  input  [7:0] B,
  output [7:0] Y
);

  wire [7:0] nor_1_out;

  nor nor_1 (nor_1_out[0], A[0], B[0]);
  nor nor_2 (nor_1_out[1], A[1], B[1]);
  nor nor_3 (nor_1_out[2], A[2], B[2]);
  nor nor_4 (nor_1_out[3], A[3], B[3]);
  nor nor_5 (nor_1_out[4], A[4], B[4]);
  nor nor_6 (nor_1_out[5], A[5], B[5]);
  nor nor_7 (nor_1_out[6], A[6], B[6]);
  nor nor_8 (nor_1_out[7], A[7], B[7]);
  buff8 buff8_1 (.enb(en_b), .A(nor_1_out), .Y(Y));
endmodule

module buf1 (
  input  enb,
  input  A,
  output Y
);

  wire en;

  not not_1 (en, enb);
  Transistor transistor_1 (.in(A), .out(Y), .gate(enb));
  Transistor #(.\type ("n")) transistor_2 (.in(A), .out(Y), .gate(en));
endmodule

module decoder2to4 (
  input  en,
  input  S0,
  input  S1,
  output A0,
  output A1,
  output A2,
  output A3
);

  wire not_1_out, not_2_out, not_3_out;

  not not_1 (not_1_out, en);
  not not_2 (not_2_out, S0);
  not not_3 (not_3_out, S1);
  nand nand_1 (A0, not_2_out, not_3_out, not_1_out);
  nand nand_2 (A1, S0, not_3_out, not_1_out);
  nand nand_3 (A2, not_2_out, S1, not_1_out);
  nand nand_4 (A3, S0, S1, not_1_out);
endmodule

module mux3x1 (
  input  s1,
  input  s0,
  input  A,
  input  B,
  input  C,
  output Y
);

  wire sb0, sb1, transmission_1_p4;

  not not_1 (sb0, s0);
  // Transmission_Gate transmission_1: pin names not known; wires that end beside it: A, s0, sb0, transmission_1_p4
  // Transmission_Gate transmission_2: pin names not known; wires that end beside it: B, s0, transmission_1_p4
  not not_2 (sb1, s1);
  // Transmission_Gate transmission_3: pin names not known; wires that end beside it: transmission_1_p4, s1, sb1, Y
  // Transmission_Gate transmission_4: pin names not known; wires that end beside it: C, s1, Y
endmodule

module mux8x3 (
  input  [7:0] A,
  input  [7:0] B,
  input  [7:0] C,
  input  [1:0] s,
  output [7:0] Y
);

  mux3x1 mux3x1_1 (.s0(s[0]), .A(A[0]), .B(B[0]), .s1(s[1]), .C(C[0]), .Y(Y[0]));
  mux3x1 mux3x1_2 (.s0(s[0]), .A(A[1]), .B(B[1]), .s1(s[1]), .C(C[1]), .Y(Y[1]));
  mux3x1 mux3x1_3 (.s0(s[0]), .A(A[2]), .B(B[2]), .s1(s[1]), .C(C[2]), .Y(Y[2]));
  mux3x1 mux3x1_4 (.s0(s[0]), .A(A[3]), .B(B[3]), .s1(s[1]), .C(C[3]), .Y(Y[3]));
  mux3x1 mux3x1_5 (.s0(s[0]), .A(A[4]), .B(B[4]), .s1(s[1]), .C(C[4]), .Y(Y[4]));
  mux3x1 mux3x1_6 (.s0(s[0]), .A(A[5]), .B(B[5]), .s1(s[1]), .C(C[5]), .Y(Y[5]));
  mux3x1 mux3x1_7 (.s0(s[0]), .A(A[6]), .B(B[6]), .s1(s[1]), .C(C[6]), .Y(Y[6]));
  mux3x1 mux3x1_8 (.s0(s[0]), .A(A[7]), .B(B[7]), .s1(s[1]), .C(C[7]), .Y(Y[7]));
endmodule

module mux3x2 (
  input  [2:0] A,
  input  [2:0] B,
  input  s,
  output [2:0] Y
);

  mux2x1 mux2x1_1 (.s(s), .A(A[0]), .B(B[0]), .Y(Y[0]));
  mux2x1 mux2x1_2 (.s(s), .A(A[1]), .B(B[1]), .Y(Y[1]));
  mux2x1 mux2x1_3 (.s(s), .A(A[2]), .B(B[2]), .Y(Y[2]));
endmodule

module comparator1bit (
  input  A,
  input  B,
  output Less,
  output Equal,
  output Greater
);

  wire not_1_out, not_2_out;

  not not_1 (not_1_out, A);
  and and_1 (Less, not_1_out, B);
  and and_2 (Greater, A, not_2_out);
  not not_2 (not_2_out, B);
  nor nor_1 (Equal, Less, Greater);

  // Notes on the sheet:
  //   A ? B
endmodule

module comparator4bit (
  input  [3:0] A,
  input  [3:0] B,
  output Less,
  output Greater,
  output Equal
);

  wire and_1_out, and_2_out, and_3_out, and_4_out, and_5_out, and_6_out, and_7_out, and_8_out,
       comparator1bit_1_equal, comparator1bit_1_greater, comparator1bit_1_less, comparator1bit_2_equal,
       comparator1bit_2_greater, comparator1bit_2_less, comparator1bit_3_equal, comparator1bit_3_greater,
       comparator1bit_3_less, comparator1bit_4_equal, comparator1bit_4_greater, comparator1bit_4_less;

  comparator1bit comparator1bit_1 (
    .A(A[3]), .B(B[3]), .Less(comparator1bit_1_less), .Equal(comparator1bit_1_equal),
    .Greater(comparator1bit_1_greater));
  comparator1bit comparator1bit_2 (
    .A(A[2]), .B(B[2]), .Less(comparator1bit_2_less), .Equal(comparator1bit_2_equal),
    .Greater(comparator1bit_2_greater));
  comparator1bit comparator1bit_3 (
    .A(A[1]), .B(B[1]), .Less(comparator1bit_3_less), .Equal(comparator1bit_3_equal),
    .Greater(comparator1bit_3_greater));
  comparator1bit comparator1bit_4 (
    .A(A[0]), .B(B[0]), .Less(comparator1bit_4_less), .Equal(comparator1bit_4_equal),
    .Greater(comparator1bit_4_greater));
  and and_1 (and_1_out, comparator1bit_1_equal, comparator1bit_2_less);
  and and_2 (and_2_out, comparator1bit_1_equal, comparator1bit_2_equal);
  and and_3 (and_3_out, and_2_out, comparator1bit_3_less);
  and and_4 (and_4_out, comparator1bit_1_equal, comparator1bit_2_greater);
  and and_5 (and_5_out, and_2_out, comparator1bit_3_greater);
  and and_6 (and_6_out, and_2_out, comparator1bit_3_equal);
  and and_7 (and_7_out, and_6_out, comparator1bit_4_less);
  and and_8 (and_8_out, and_6_out, comparator1bit_4_greater);
  and and_9 (Equal, and_6_out, comparator1bit_4_equal);
  or or_1 (Less, comparator1bit_1_less, and_1_out, and_3_out, and_7_out);
  or or_2 (Greater, comparator1bit_1_greater, and_4_out, and_5_out, and_8_out);
endmodule

module comparator8bit (
  input  [7:0] B,
  input  [7:0] A,
  input  enb,
  output [7:0] GEL
);

  wire aoi_1_y, aoi_2_y, comparator4bit_1_equal, comparator4bit_1_greater, comparator4bit_1_less,
       comparator4bit_2_equal, comparator4bit_2_greater, comparator4bit_2_less;
  wire [2:0] not_1_out;

  comparator4bit comparator4bit_1 (
    .A(A[3:0]), .B(B[3:0]), .Equal(comparator4bit_1_equal), .Less(comparator4bit_1_less),
    .Greater(comparator4bit_1_greater));
  comparator4bit comparator4bit_2 (
    .A(A[7:4]), .B(B[7:4]), .Equal(comparator4bit_2_equal), .Less(comparator4bit_2_less),
    .Greater(comparator4bit_2_greater));
  not not_1 (not_1_out[0], aoi_1_y);
  aoi aoi_1 (.C(comparator4bit_2_equal), .A(comparator4bit_2_less), .B(comparator4bit_1_less), .Y(aoi_1_y));
  aoi aoi_2 (.C(comparator4bit_2_equal), .A(comparator4bit_2_greater), .B(comparator4bit_1_greater), .Y(aoi_2_y));
  and and_1 (not_1_out[1], comparator4bit_2_equal, comparator4bit_1_equal);
  not not_2 (not_1_out[2], aoi_2_y);
  buff8 buff8_1 (.enb(enb), .A({{5{1'b0}}, not_1_out}), .Y(GEL));

  // Notes on the sheet:
  //   A ? B
endmodule

module EqualityDetector (
  input  [7:0] A,
  input  [7:0] B,
  output Equal
);

  wire xor2_1_y, xor2_2_y, xor2_3_y, xor2_4_y, xor2_5_y, xor2_6_y, xor2_7_y, xor2_8_y;

  XOR2 xor2_1 (.A(A[0]), .B(B[0]), .Y(xor2_1_y));
  XOR2 xor2_2 (.A(A[1]), .B(B[1]), .Y(xor2_2_y));
  XOR2 xor2_3 (.A(A[2]), .B(B[2]), .Y(xor2_3_y));
  XOR2 xor2_4 (.A(A[3]), .B(B[3]), .Y(xor2_4_y));
  XOR2 xor2_5 (.A(A[4]), .B(B[4]), .Y(xor2_5_y));
  XOR2 xor2_6 (.A(A[5]), .B(B[5]), .Y(xor2_6_y));
  XOR2 xor2_7 (.A(A[6]), .B(B[6]), .Y(xor2_7_y));
  XOR2 xor2_8 (.A(A[7]), .B(B[7]), .Y(xor2_8_y));
  nor nor_1 (Equal, xor2_1_y, xor2_2_y, xor2_3_y, xor2_4_y, xor2_5_y, xor2_6_y, xor2_7_y, xor2_8_y);
endmodule
