// Logisim project Reg.circ as structural Verilog: 14 circuits, main circuit oai
module oai (
  input  A,
  input  B,
  input  C,
  output Y
);

  wire transistor_1_out, transistor_4_out;

  Transistor transistor_1 (.in(1'b1), .out(transistor_1_out), .gate(B));
  Transistor transistor_2 (.in(transistor_1_out), .out(Y), .gate(C));
  Transistor #(.\type ("n")) transistor_3 (.in(transistor_4_out), .out(Y), .gate(C));
  Transistor #(.\type ("n")) transistor_4 (.in(1'b0), .out(transistor_4_out), .gate(A));
  Transistor transistor_5 (.in(1'b1), .out(Y), .gate(A));
  Transistor #(.\type ("n")) transistor_6 (.in(transistor_4_out), .out(Y), .gate(B));
endmodule

module aoi (
  input  A,
  input  B,
  input  C,
  output Y
);

  wire transistor_1_out, transistor_6_out;

  Transistor transistor_1 (.in(1'b1), .out(transistor_1_out), .gate(B));
  Transistor transistor_2 (.in(transistor_1_out), .out(Y), .gate(A));
  Transistor #(.\type ("n")) transistor_3 (.in(1'b0), .out(Y), .gate(A));
  Transistor transistor_4 (.in(1'b1), .out(transistor_1_out), .gate(C));
  Transistor #(.\type ("n")) transistor_5 (.in(transistor_6_out), .out(Y), .gate(C));
  Transistor #(.\type ("n")) transistor_6 (.in(1'b0), .out(transistor_6_out), .gate(B));
endmodule

module dff (
  input  D,
  input  CLK,
  output Q,
  output Qb
);

  wire and_1_out, and_2_out, nand_1_out, nand_2_out, not_1_out, or_1_out, or_2_out;

  not not_1 (not_1_out, D);
  or or_1 (or_1_out, CLK, D);
  or or_2 (or_2_out, not_1_out, CLK);
  nand nand_1 (nand_1_out, or_1_out, nand_2_out);
  nand nand_2 (nand_2_out, nand_1_out, or_2_out);
  and and_1 (and_1_out, nand_1_out, CLK);
  and and_2 (and_2_out, nand_2_out, CLK);
  nor nor_1 (Q, and_1_out, Qb);
  nor nor_2 (Qb, Q, and_2_out);

  // Notes on the sheet:
  //   Make sure to disconnect and reconnect the wires to make them reset
  //   The oai and aoi for some reason doesn't work so I used used logic gates instead of transistors
endmodule

module mux2x1 (
  input  s,
  input  A,
  input  B,
  output Y
);

  wire sb;

  not not_1 (sb, s);
  // Transmission_Gate transmission_1: pin names not known; wires that end beside it: A, s, sb, Y
  // Transmission_Gate transmission_2: pin names not known; wires that end beside it: B, s, Y
endmodule

module mux8x2 (
  input  [7:0] A,
  input  [7:0] B,
  input  S,
  output [7:0] Y
);

  mux2x1 mux2x1_1 (.s(S), .A(A[0]), .B(B[0]), .Y(Y[0]));
  mux2x1 mux2x1_2 (.s(S), .A(A[1]), .B(B[1]), .Y(Y[1]));
  mux2x1 mux2x1_3 (.s(S), .A(A[2]), .B(B[2]), .Y(Y[2]));
  mux2x1 mux2x1_4 (.s(S), .A(A[3]), .B(B[3]), .Y(Y[3]));
  mux2x1 mux2x1_5 (.s(S), .A(A[4]), .B(B[4]), .Y(Y[4]));
  mux2x1 mux2x1_6 (.s(S), .A(A[5]), .B(B[5]), .Y(Y[5]));
  mux2x1 mux2x1_7 (.s(S), .A(A[6]), .B(B[6]), .Y(Y[6]));
  mux2x1 mux2x1_8 (.s(S), .A(A[7]), .B(B[7]), .Y(Y[7]));
endmodule

module reg8 (
  input  [7:0] D,
  input  clk,
  output [7:0] Q
);

  wire [7:0] dff_1_qb;

  dff dff_1 (.D(D[0]), .CLK(clk), .Q(Q[0]), .Qb(dff_1_qb[0]));
  dff dff_2 (.D(D[1]), .CLK(clk), .Q(Q[1]), .Qb(dff_1_qb[1]));
  dff dff_3 (.D(D[2]), .CLK(clk), .Q(Q[2]), .Qb(dff_1_qb[2]));
  dff dff_4 (.D(D[3]), .CLK(clk), .Q(Q[3]), .Qb(dff_1_qb[3]));
  dff dff_5 (.D(D[4]), .CLK(clk), .Q(Q[4]), .Qb(dff_1_qb[4]));
  dff dff_6 (.D(D[5]), .CLK(clk), .Q(Q[5]), .Qb(dff_1_qb[5]));
  dff dff_7 (.D(D[6]), .CLK(clk), .Q(Q[6]), .Qb(dff_1_qb[6]));
  dff dff_8 (.D(D[7]), .CLK(clk), .Q(Q[7]), .Qb(dff_1_qb[7]));

  // Notes on the sheet:
  //   Make sure to tick clk once
endmodule

module reg8withmux (
  input  [7:0] D,
  input  clk,
  input  en,
  output [7:0] Q
);

  wire [7:0] mux8x2_1_y;

  mux8x2 mux8x2_1 (.B(D), .A(Q), .S(en), .Y(mux8x2_1_y));
  reg8 reg8_1 (.D(mux8x2_1_y), .clk(clk), .Q(Q));

  // Notes on the sheet:
  //   Make sure to initialize it by ticking en and clk
endmodule

module buff8 (
  input  [7:0] A,
  input  enb,
  output [7:0] Y
);

  wire en;

  Transistor transistor_1 (.in(A[7]), .out(Y[7]), .gate(enb));
  Transistor #(.\type ("n")) transistor_2 (.in(A[7]), .out(Y[7]), .gate(en));
  not not_1 (en, enb);
  Transistor transistor_3 (.in(A[6]), .out(Y[6]), .gate(enb));
  Transistor #(.\type ("n")) transistor_4 (.in(A[6]), .out(Y[6]), .gate(en));
  Transistor transistor_5 (.in(A[5]), .out(Y[5]), .gate(enb));
  Transistor #(.\type ("n")) transistor_6 (.in(A[5]), .out(Y[5]), .gate(en));
  Transistor transistor_7 (.in(A[4]), .out(Y[4]), .gate(enb));
  Transistor #(.\type ("n")) transistor_8 (.in(A[4]), .out(Y[4]), .gate(en));
  Transistor transistor_9 (.in(A[3]), .out(Y[3]), .gate(enb));
  Transistor #(.\type ("n")) transistor_10 (.in(A[3]), .out(Y[3]), .gate(en));
  Transistor transistor_11 (.in(A[2]), .out(Y[2]), .gate(enb));
  Transistor #(.\type ("n")) transistor_12 (.in(A[2]), .out(Y[2]), .gate(en));
  Transistor transistor_13 (.in(A[1]), .out(Y[1]), .gate(enb));
  Transistor #(.\type ("n")) transistor_14 (.in(A[1]), .out(Y[1]), .gate(en));
  Transistor transistor_15 (.in(A[0]), .out(Y[0]), .gate(enb));
  Transistor #(.\type ("n")) transistor_16 (.in(A[0]), .out(Y[0]), .gate(en));
endmodule

module regi (
  input  clk,
  input  [7:0] C,
  input  b_en,
  input  reg_en,
  input  a_en,
  output [7:0] Q,
  output [7:0] B,
  output [7:0] A
);

  reg8withmux reg8withmux_1 (.D(C), .en(reg_en), .clk(clk), .Q(Q));
  buff8 buff8_1 (.enb(b_en), .A(Q), .Y(B));
  buff8 buff8_2 (.enb(a_en), .A(Q), .Y(A));

  // Notes on the sheet:
  //   Make sure to initialize it by ticking reg_en and clk
endmodule

module regi0 (
  input  b_en,
  input  a_en,
  output [7:0] Q,
  output [7:0] B,
  output [7:0] A
);

  buff8 buff8_1 (.enb(b_en), .A({8{1'b0}}), .Y(B));
  buff8 buff8_2 (.enb(a_en), .A({8{1'b0}}), .Y(A));

  assign Q = {8{1'b0}};
endmodule

module decode (
  input  en,
  input  S0,
  input  S1,
  input  S2,
  output A0,
  output A1,
  output A2,
  output A3,
  output A4,
  output A5,
  output A6,
  output A7
);

  wire not_1_out, not_2_out, not_3_out, not_4_out;

  not not_1 (not_1_out, en);
  not not_2 (not_2_out, S0);
  not not_3 (not_3_out, S1);
  not not_4 (not_4_out, S2);
  nand nand_1 (A0, not_2_out, not_3_out, not_4_out, not_1_out);
  nand nand_2 (A1, S0, not_3_out, not_4_out, not_1_out);
  nand nand_3 (A2, not_2_out, S1, not_4_out, not_1_out);
  nand nand_4 (A3, S0, S1, not_4_out, not_1_out);
  nand nand_5 (A4, not_2_out, not_3_out, S2, not_1_out);
  nand nand_6 (A5, S0, not_3_out, S2, not_1_out);
  nand nand_7 (A6, not_2_out, S1, S2, not_1_out);
  nand nand_8 (A7, S0, S1, S2, not_1_out);
endmodule

module decode_inv (
  input  en,
  input  S0,
  input  S1,
  input  S2,
  output A0,
  output A1,
  output A2,
  output A3,
  output A4,
  output A5,
  output A6,
  output A7
);

  wire not_1_out, not_2_out, not_3_out, not_4_out;

  not not_1 (not_1_out, en);
  not not_2 (not_2_out, S0);
  not not_3 (not_3_out, S1);
  not not_4 (not_4_out, S2);
  and and_1 (A0, not_2_out, not_3_out, not_4_out, not_1_out);
  and and_2 (A1, S0, not_3_out, not_4_out, not_1_out);
  and and_3 (A2, not_2_out, S1, not_4_out, not_1_out);
  and and_4 (A3, S0, S1, not_4_out, not_1_out);
  and and_5 (A4, not_2_out, not_3_out, S2, not_1_out);
  and and_6 (A5, S0, not_3_out, S2, not_1_out);
  and and_7 (A6, not_2_out, S1, S2, not_1_out);
  and and_8 (A7, S0, S1, S2, not_1_out);
endmodule

module register_file (
  input  [7:0] C,
  input  [7:0] Imm,
  input  immediate_en,
  input  [3:0] C_sel,
  input  [2:0] B_sel,
  input  [2:0] A_sel,
  input  clk,
  output [7:0] B,
  output [7:0] A
);

  wire a_en_a0, a_en_a1, a_en_a2, a_en_a3, a_en_a4, a_en_a5, a_en_a6, a_en_a7, b_en_a0, b_en_a1, b_en_a2,
       b_en_a3, b_en_a4, b_en_a5, b_en_a6, b_en_a7, decode_inv_1_a0, decode_inv_1_a1, decode_inv_1_a2,
       decode_inv_1_a3, decode_inv_1_a4, decode_inv_1_a5, decode_inv_1_a6;
  wire [7:0] mux8x2_1_y, regi0_1_q, regi_1_q, regi_2_q, regi_3_q, regi_4_q, regi_5_q, regi_6_q, regi_7_q;

  decode a_en (
    .en(1'b0), .S0(A_sel[0]), .S1(A_sel[1]), .S2(A_sel[2]), .A0(a_en_a0), .A1(a_en_a1), .A2(a_en_a2),
    .A3(a_en_a3), .A4(a_en_a4), .A5(a_en_a5), .A6(a_en_a6), .A7(a_en_a7));
  decode b_en (
    .en(1'b0), .S0(B_sel[0]), .S1(B_sel[1]), .S2(B_sel[2]), .A0(b_en_a0), .A1(b_en_a1), .A2(b_en_a2),
    .A3(b_en_a3), .A4(b_en_a4), .A5(b_en_a5), .A6(b_en_a6), .A7(b_en_a7));
  mux8x2 mux8x2_1 (.B(Imm), .A(C), .S(immediate_en), .Y(mux8x2_1_y));
  decode_inv decode_inv_1 (
    .en(C_sel[3]), .S0(C_sel[0]), .S1(C_sel[1]), .S2(C_sel[2]), .A0(decode_inv_1_a0), .A1(decode_inv_1_a1),
    .A2(decode_inv_1_a2), .A3(decode_inv_1_a3), .A4(decode_inv_1_a4), .A5(decode_inv_1_a5),
    .A6(decode_inv_1_a6));  // open: A7
  regi regi_1 (
    .C(mux8x2_1_y), .clk(clk), .reg_en(decode_inv_1_a0), .b_en(b_en_a0), .a_en(a_en_a0), .Q(regi_1_q), .B(B),
    .A(A));
  regi regi_2 (
    .C(mux8x2_1_y), .clk(clk), .reg_en(decode_inv_1_a1), .b_en(b_en_a1), .a_en(a_en_a1), .Q(regi_2_q), .B(B),
    .A(A));
  regi regi_3 (
    .C(mux8x2_1_y), .clk(clk), .reg_en(decode_inv_1_a2), .b_en(b_en_a2), .a_en(a_en_a2), .Q(regi_3_q), .B(B),
    .A(A));
  regi regi_4 (
    .C(mux8x2_1_y), .clk(clk), .reg_en(decode_inv_1_a3), .b_en(b_en_a3), .a_en(a_en_a3), .Q(regi_4_q), .B(B),
    .A(A));
  regi regi_5 (
    .C(mux8x2_1_y), .clk(clk), .reg_en(decode_inv_1_a4), .b_en(b_en_a4), .a_en(a_en_a4), .Q(regi_5_q), .B(B),
    .A(A));
  regi regi_6 (
    .C(mux8x2_1_y), .clk(clk), .reg_en(decode_inv_1_a5), .b_en(b_en_a5), .a_en(a_en_a5), .Q(regi_6_q), .B(B),
    .A(A));
  regi regi_7 (
    .C(mux8x2_1_y), .clk(clk), .reg_en(decode_inv_1_a6), .b_en(b_en_a6), .a_en(a_en_a6), .Q(regi_7_q), .B(B),
    .A(A));
  regi0 regi0_1 (.b_en(b_en_a7), .a_en(a_en_a7), .Q(regi0_1_q), .B(B), .A(A));
  // Probe on regi_1_q
  // Probe on regi_2_q
  // Probe on regi_3_q
  // Probe on regi_4_q
  // Probe on regi_5_q
  // Probe on regi_6_q
  // Probe on regi_7_q
  // Probe on regi0_1_q

  // Notes on the sheet:
  //   Make sure to initialize it by ticking C_sel and clk
endmodule

module main (
  input  [3:0] csel,
  input  [2:0] bsel,
  input  [2:0] asel,
  input  [7:0] C,
  input  [7:0] Imm,
  input  clk,
  input  imm_en
);

  wire [7:0] register_file_1_a, register_file_1_b;

  register_file register_file_1 (
    .A_sel(asel), .C_sel(csel), .B_sel(bsel), .immediate_en(imm_en), .Imm(C), .C(Imm), .clk(clk),
    .B(register_file_1_b), .A(register_file_1_a));
  // Probe on register_file_1_a
  // Probe on register_file_1_b

  // Notes on the sheet:
  //   Make sure to initialize it by ticking C_sel and clk
endmodule
